# Fritzing sketch air_state_sensor (saved by Fritzing 0.9.3b)
breadboards: 1

parts:
  WeMos_D1_Mini1 = WeMos D1 Mini
  AM1 = AM2302 Humidity and Temperature Sensor

nets:
  3V3: WeMos_D1_Mini1.3V3, AM1.VDD
  N1: WeMos_D1_Mini1.D2, AM1.DATA
  N2: WeMos_D1_Mini1.G, AM1.GND
